// Logisim project ex5.circ as structural Verilog: 5 circuits, main circuit rotr
module rotr (
  input  [15:0] A,
  input  [3:0] B,
  output [15:0] Out1
);

  wire [15:0] DATA1, DATA2, DATA3, rot1_1_out_2, rot2_1_out_2, rot4_1_out_2, rot8_1_out_2;

  Multiplexer #(.enable("false"), .width(16)) multiplexer_1 (.in0(DATA2), .in1(rot4_1_out_2), .out(DATA3), .sel(B[2]));
  rot4 rot4_1 (.in_1(DATA2), .out_2(rot4_1_out_2));
  Multiplexer #(.enable("false"), .width(16)) multiplexer_2 (.in0(A), .in1(rot1_1_out_2), .out(DATA1), .sel(B[0]));
  rot1 rot1_1 (.in_1(A), .out_2(rot1_1_out_2));
  rot8 rot8_1 (.in_1(DATA3), .out_2(rot8_1_out_2));
  Multiplexer #(.enable("false"), .width(16)) multiplexer_3 (.in0(DATA3), .in1(rot8_1_out_2), .out(Out1), .sel(B[3]));
  Multiplexer #(.enable("false"), .width(16)) multiplexer_4 (.in0(DATA1), .in1(rot2_1_out_2), .out(DATA2), .sel(B[1]));
  rot2 rot2_1 (.in_1(DATA1), .out_2(rot2_1_out_2));

  // Other names for the same wires on the sheet: ONE = B[0]; TWO = B[1]; THR = B[2]; FOU = B[3]; DATA[15:0] = A;
  //   RES[15:0] = Out1

  // Notes on the sheet:
  //   PUT CIRCUITRY HERE
endmodule

module rot8 (
  input  [15:0] in_1,
  output [15:0] out_2
);

  wire [15:0] rot4_1_out_2;

  rot4 rot4_1 (.in_1(in_1), .out_2(rot4_1_out_2));
  rot4 rot4_2 (.in_1(rot4_1_out_2), .out_2(out_2));

  // Notes on the sheet:
  //   PUT CIRCUITRY HERE
endmodule

module rot4 (
  input  [15:0] in_1,
  output [15:0] out_2
);

  wire [15:0] rot2_1_out_2;

  rot2 rot2_1 (.in_1(in_1), .out_2(rot2_1_out_2));
  rot2 rot2_2 (.in_1(rot2_1_out_2), .out_2(out_2));

  // Notes on the sheet:
  //   PUT CIRCUITRY HERE
endmodule

module rot2 (
  input  [15:0] in_1,
  output [15:0] out_2
);

  wire [15:0] rot1_1_out_2;

  rot1 rot1_1 (.in_1(in_1), .out_2(rot1_1_out_2));
  rot1 rot1_2 (.in_1(rot1_1_out_2), .out_2(out_2));

  // Notes on the sheet:
  //   PUT CIRCUITRY HERE
endmodule

module rot1 (
  input  [15:0] in_1,
  output [15:0] out_2
);


  assign out_2 = {in_1[0], in_1[15:1]};

  // Other names for the same wires on the sheet: LAR[14:0] = in_1[15:1]; ONE = in_1[0]

  // Notes on the sheet:
  //   PUT CIRCUITRY HERE
endmodule
