// Logisim project branch_comp.circ as structural Verilog: 1 circuit, main circuit branch_comp
module branch_comp (
  input  [31:0] rs1,
  input  [31:0] rs2,
  input  BrUn,
  output BrEq,
  output BrLt
);

  wire breq_t, brequ, brlt_t, brltu;

  Comparator #(.mode("unsigned"), .width(32)) comparator_1 (.a(rs1), .b(rs2), .eq(brequ), .lt(brltu));  // open: gt
  Comparator #(.width(32)) comparator_2 (.a(rs1), .b(rs2), .eq(breq_t), .lt(brlt_t));  // open: gt
  Multiplexer #(.enable("false")) multiplexer_1 (.in0(breq_t), .in1(brequ), .out(BrEq), .sel(BrUn));
  Multiplexer #(.enable("false")) multiplexer_2 (.in0(brlt_t), .in1(brltu), .out(BrLt), .sel(BrUn));

  // Notes on the sheet:
  //   INPUTS to your circuit
  //   DON'T CHANGE THE LOCATIONS OF THE INPUTS AND OUTPUTS!
  //   OUTPUT from your circuit
endmodule
