// Logisim project control_logic.circ as structural Verilog: 1 circuit, main circuit control_logic
module control_logic (
  input  [31:0] inst,
  input  BrEq,
  input  BrLt,
  output PCSel,
  output RegWEn,
  output [2:0] ImmSel,
  output BrUn,
  output ASel,
  output BSel,
  output [3:0] ALUSel,
  output MemRW,
  output [1:0] WBSel,
  output CSRSel,
  output CSRWen
);

  wire ALU_WB, AUI_type, B_ALU, B_type, BEQ, BEQ_ALU, BGE, BGE_ALU, BGEU, BGEU_ALU, BLT, BLT_ALU, BLTU,
       BLTU_ALU, BNE, BNE_ALU, CL_BSEL, I_type, Imm_0, Imm_3, Imm_4, JALR_type, L_AND, L_OR, L_SLL, L_SLT,
       L_SRA, L_SRL, L_type, L_XOR, LUI_type, not_18_out, not_19_out, not_20_out, not_five, not_four,
       not_func3_one, not_func3_three, not_func3_two, not_func7_five, not_func7_four, not_func7_one,
       not_func7_seven, not_func7_six, not_func7_three, not_func7_two, not_one, not_six, not_three, not_two,
       not_zero, PC_WB, R_AND, R_MUL, R_MULH, R_MULHU, R_OR, R_SLL, R_SLT, R_SRA, R_SRL, R_SUB, R_type,
       R_XOR, RV32I, T_AND, T_OR, T_SLL, T_SLT, T_SRA, T_SRL, T_XOR;
  wire [1:0] WB_ADD1, WB_ALU, WB_MEM, WB_PC;
  wire [2:0] Imm_add0, Imm_ADD1, Imm_add1_t, Imm_ADD2, Imm_add2_t, Imm_ADD3, Imm_add3_t, Imm_ADD4,
       Imm_add4_t, Imm_add5;
  wire [3:0] ALU_add_0, ALU_ADD_1, ALU_add_1_t, ALU_ADD_2, ALU_add_2_t, ALU_ADD_3, ALU_add_3_t, ALU_ADD_4,
       ALU_add_4_t, ALU_ADD_5, ALU_add_5_t, ALU_ADD_6, ALU_add_6_t, ALU_ADD_7, ALU_add_7_t, ALU_ADD_8,
       ALU_add_8_t, ALU_ADD_9, ALU_add_9_t, ALU_ADD_10, ALU_add_10_t, ALU_add_11;

  not not_1 (not_zero, inst[0]);
  not not_2 (not_one, inst[1]);
  not not_3 (not_two, inst[2]);
  not not_4 (not_three, inst[3]);
  not not_5 (not_four, inst[4]);
  not not_6 (not_five, inst[5]);
  not not_7 (not_six, inst[6]);
  not not_8 (not_func7_one, inst[25]);
  not not_9 (not_func7_two, inst[26]);
  not not_10 (not_func7_three, inst[27]);
  not not_11 (not_func7_four, inst[28]);
  not not_12 (not_func7_five, inst[29]);
  not not_13 (not_func7_six, inst[30]);
  not not_14 (not_func7_seven, inst[31]);
  not not_15 (not_func3_one, inst[12]);
  not not_16 (not_func3_two, inst[13]);
  not not_17 (not_func3_three, inst[14]);
  not not_18 (not_18_out, BrEq);
  not not_19 (not_19_out, BrLt);
  not not_20 (not_20_out, BrLt);
  and and_1 (BEQ_ALU, BEQ, BrEq);
  and and_2 (BLT_ALU, BLT, BrLt);
  and and_3 (BNE_ALU, BNE, not_18_out);
  and and_4 (BGE_ALU, BGE, not_19_out);
  and and_5 (BLTU_ALU, BLTU, BrLt);
  and and_6 (BGEU_ALU, BGEU, not_20_out);
  and and_7 (RV32I, inst[0], inst[1]);
  and and_8 (BrUn, B_type, inst[13], inst[14]);
  and and_9 (R_type, inst[4], not_two, not_three, inst[5], not_six, RV32I);
  and and_10 (L_type, RV32I, not_two, not_three, not_four, not_five, not_six);
  or or_1 (RegWEn, R_type, L_type, I_type, Imm_3, JALR_type, AUI_type, LUI_type);
  and and_11 (I_type, RV32I, not_two, not_three, inst[4], not_five, not_six);
  and and_12 (MemRW, RV32I, not_two, not_three, not_four, inst[5], not_six);
  and and_13 (B_type, RV32I, not_two, not_three, not_four, inst[5], inst[6]);
  and and_14 (CSRWen, RV32I, not_two, not_three, inst[4], inst[5], inst[6]);
  and and_15 (JALR_type, RV32I, inst[2], not_three, not_four, inst[5], inst[6]);
  and and_16 (Imm_3, RV32I, inst[2], inst[3], not_four, inst[5], inst[6]);
  and and_17 (LUI_type, RV32I, inst[2], not_three, inst[4], inst[5], not_six);
  and and_18 (AUI_type, RV32I, inst[2], not_three, inst[4], not_five, not_six);
  not not_21 (BSel, R_type);
  Multiplexer #(.enable("false"), .width(3)) multiplexer_1 (.in0(3'b000), .in1(3'b101), .out(Imm_add5), .sel(CSRWen));
  or or_2 (B_ALU, BEQ_ALU, BLT_ALU, BNE_ALU, BGE_ALU, BLTU_ALU, BGEU_ALU);
  or or_3 (PCSel, B_ALU, JALR_type, Imm_3);
  or or_4 (ASel, L_type, R_type, I_type, MemRW, JALR_type);
  and and_19 (BGE, B_type, inst[12], not_func3_two, inst[14]);
  and and_20 (BNE, B_type, inst[12], not_func3_two, not_func3_three);
  and and_21 (BLT, B_type, not_func3_one, not_func3_two, inst[14]);
  and and_22 (BEQ, B_type, not_func3_one, not_func3_two, not_func3_three);
  or or_5 (Imm_4, AUI_type, LUI_type);
  Multiplexer #(.enable("false"), .width(3)) multiplexer_2 (.in0(3'b000), .in1(3'b000), .out(Imm_add0), .sel(Imm_0));
  Multiplexer #(.enable("false"), .width(3)) multiplexer_3 (.in0(3'b000), .in1(3'b001), .out(Imm_add1_t), .sel(MemRW));
  Multiplexer #(.enable("false"), .width(3)) multiplexer_4 (.in0(3'b000), .in1(3'b010), .out(Imm_add2_t), .sel(B_type));
  Multiplexer #(.enable("false"), .width(3)) multiplexer_5 (.in0(3'b000), .in1(3'b011), .out(Imm_add3_t), .sel(Imm_3));
  Multiplexer #(.enable("false"), .width(3)) multiplexer_6 (.in0(3'b000), .in1(3'b100), .out(Imm_add4_t), .sel(Imm_4));
  and and_23 (BLTU, B_type, not_func3_one, inst[13], inst[14]);
  or or_6 (Imm_0, I_type, L_type, JALR_type);
  Adder #(.width(3)) adder_1 (.a(Imm_add0), .b(Imm_add1_t), .out(Imm_ADD1));  // open: cin, cout
  Adder #(.width(3)) adder_2 (.a(Imm_ADD1), .b(Imm_add2_t), .out(Imm_ADD2));  // open: cin, cout
  Adder #(.width(3)) adder_3 (.a(Imm_ADD2), .b(Imm_add3_t), .out(Imm_ADD3));  // open: cin, cout
  Adder #(.width(3)) adder_4 (.a(Imm_ADD4), .b(Imm_add5), .out(ImmSel));  // open: cin, cout
  Adder #(.width(3)) adder_5 (.a(Imm_ADD3), .b(Imm_add4_t), .out(Imm_ADD4));  // open: cin, cout
  and and_24 (BGEU, B_type, inst[12], inst[13], inst[14]);
  or or_7 (PC_WB, JALR_type, Imm_3);
  Multiplexer #(.enable("false"), .width(2)) multiplexer_7 (.in0(2'b00), .in1(2'b00), .out(WB_PC), .sel(PC_WB));
  Multiplexer #(.enable("false"), .width(2)) multiplexer_8 (.in0(2'b00), .in1(2'b01), .out(WB_ALU), .sel(ALU_WB));
  Multiplexer #(.enable("false"), .width(2)) multiplexer_9 (.in0(2'b00), .in1(2'b10), .out(WB_MEM), .sel(L_type));
  Adder #(.width(2)) adder_6 (.a(WB_PC), .b(WB_ALU), .out(WB_ADD1));  // open: cin, cout
  Adder #(.width(2)) adder_7 (.a(WB_ADD1), .b(WB_MEM), .out(WBSel));  // open: cin, cout
  or or_8 (ALU_WB, R_type, I_type, LUI_type, AUI_type);
  and and_25 (R_SUB, R_type, not_func3_one, not_func3_two, not_func3_three, inst[30], not_func7_one);
  and and_26 (R_MUL, R_type, not_func3_one, not_func3_two, not_func3_three, not_func7_six, inst[25]);
  and and_27 (R_MULH, R_type, inst[12], not_func3_two, not_func3_three, not_func7_six, inst[25]);
  and and_28 (R_MULHU, R_type, inst[12], inst[13], not_func3_three, not_func7_six, inst[25]);
  and and_29 (L_SLL, I_type, inst[12], not_func3_two, not_func3_three);
  and and_30 (L_SLT, I_type, not_func3_one, inst[13], not_func3_three);
  and and_31 (L_XOR, I_type, not_func3_one, not_func3_two, inst[14]);
  and and_32 (L_OR, I_type, not_func3_one, inst[13], inst[14]);
  and and_33 (L_AND, I_type, inst[12], inst[13], inst[14]);
  and and_34 (R_SLL, R_type, inst[12], not_func3_two, not_func3_three, not_func7_six, not_func7_one);
  and and_35 (L_SRL, I_type, inst[12], not_func3_two, inst[14], not_func7_six, not_func7_one);
  and and_36 (L_SRA, I_type, inst[12], not_func3_two, inst[14], inst[30], not_func7_one);
  and and_37 (R_SLT, R_type, not_func3_one, inst[13], not_func3_three, not_func7_six, not_func7_one);
  and and_38 (R_XOR, R_type, not_func3_one, not_func3_two, inst[14], not_func7_six, not_func7_one);
  and and_39 (R_SRL, R_type, inst[12], not_func3_two, inst[14], not_func7_six, not_func7_one);
  and and_40 (R_SRA, R_type, inst[12], not_func3_two, inst[14], inst[30], not_func7_one);
  and and_41 (R_OR, R_type, not_func3_one, inst[13], inst[14], not_func7_six, not_func7_one);
  and and_42 (R_AND, R_type, inst[12], inst[13], inst[14], not_func7_six, not_func7_one);
  or or_9 (T_SLL, L_SLL, R_SLL);
  or or_10 (T_SLT, L_SLT, R_SLT);
  or or_11 (T_XOR, L_XOR, R_XOR);
  or or_12 (T_OR, L_OR, R_OR);
  or or_13 (T_AND, L_AND, R_AND);
  or or_14 (T_SRL, L_SRL, R_SRL);
  or or_15 (T_SRA, L_SRA, R_SRA);
  or or_16 (CL_BSEL, CSRWen, LUI_type);
  Multiplexer #(.enable("false"), .width(4)) multiplexer_10 (
    .in0(4'b0000), .in1(4'b0110), .out(ALU_add_0), .sel(T_SLL));
  Multiplexer #(.enable("false"), .width(4)) multiplexer_11 (
    .in0(4'b0000), .in1(4'b0111), .out(ALU_add_1_t), .sel(T_SLT));
  Multiplexer #(.enable("false"), .width(4)) multiplexer_12 (
    .in0(4'b0000), .in1(4'b0011), .out(ALU_add_2_t), .sel(T_XOR));
  Multiplexer #(.enable("false"), .width(4)) multiplexer_13 (
    .in0(4'b0000), .in1(4'b0010), .out(ALU_add_3_t), .sel(T_OR));
  Multiplexer #(.enable("false"), .width(4)) multiplexer_14 (
    .in0(4'b0000), .in1(4'b0001), .out(ALU_add_4_t), .sel(T_AND));
  Multiplexer #(.enable("false"), .width(4)) multiplexer_15 (
    .in0(4'b0000), .in1(4'b0100), .out(ALU_add_5_t), .sel(T_SRL));
  Multiplexer #(.enable("false"), .width(4)) multiplexer_16 (
    .in0(4'b0000), .in1(4'b0101), .out(ALU_add_6_t), .sel(T_SRA));
  Multiplexer #(.enable("false"), .width(4)) multiplexer_17 (
    .in0(4'b0000), .in1(4'b1010), .out(ALU_add_7_t), .sel(R_MUL));
  Multiplexer #(.enable("false"), .width(4)) multiplexer_18 (
    .in0(4'b0000), .in1(4'b1011), .out(ALU_add_8_t), .sel(R_MULHU));
  Multiplexer #(.enable("false"), .width(4)) multiplexer_19 (
    .in0(4'b0000), .in1(4'b1100), .out(ALU_add_9_t), .sel(R_SUB));
  Multiplexer #(.enable("false"), .width(4)) multiplexer_20 (
    .in0(4'b0000), .in1(4'b1101), .out(ALU_add_10_t), .sel(CL_BSEL));
  Multiplexer #(.enable("false"), .width(4)) multiplexer_21 (
    .in0(4'b0000), .in1(4'b1110), .out(ALU_add_11), .sel(R_MULH));
  Adder #(.width(4)) adder_8 (.a(ALU_add_0), .b(ALU_add_1_t), .out(ALU_ADD_1));  // open: cin, cout
  Adder #(.width(4)) adder_9 (.a(ALU_ADD_1), .b(ALU_add_2_t), .out(ALU_ADD_2));  // open: cin, cout
  Adder #(.width(4)) adder_10 (.a(ALU_ADD_2), .b(ALU_add_3_t), .out(ALU_ADD_3));  // open: cin, cout
  Adder #(.width(4)) adder_11 (.a(ALU_ADD_3), .b(ALU_add_4_t), .out(ALU_ADD_4));  // open: cin, cout
  Adder #(.width(4)) adder_12 (.a(ALU_ADD_4), .b(ALU_add_5_t), .out(ALU_ADD_5));  // open: cin, cout
  Adder #(.width(4)) adder_13 (.a(ALU_ADD_5), .b(ALU_add_6_t), .out(ALU_ADD_6));  // open: cin, cout
  Adder #(.width(4)) adder_14 (.a(ALU_ADD_6), .b(ALU_add_7_t), .out(ALU_ADD_7));  // open: cin, cout
  Adder #(.width(4)) adder_15 (.a(ALU_ADD_7), .b(ALU_add_8_t), .out(ALU_ADD_8));  // open: cin, cout
  Adder #(.width(4)) adder_16 (.a(ALU_ADD_8), .b(ALU_add_9_t), .out(ALU_ADD_9));  // open: cin, cout
  Adder #(.width(4)) adder_17 (.a(ALU_ADD_9), .b(ALU_add_10_t), .out(ALU_ADD_10));  // open: cin, cout
  Adder #(.width(4)) adder_18 (.a(ALU_ADD_10), .b(ALU_add_11), .out(ALUSel));  // open: cin, cout

  assign CSRSel = inst[14];

  // Other names for the same wires on the sheet: Imm_2 = B_type; CSR_type = CSRWen; Imm_5 = CSRWen; zero = inst[0];
  //   one = inst[1]; two = inst[2]; three = inst[3]; four = inst[4]; five = inst[5]; six = inst[6];
  //   func3_one = inst[12]; func3_two = inst[13]; func3_three = inst[14]; func7_one = inst[25]; func7_two = inst[26];
  //   func7_three = inst[27]; func7_four = inst[28]; func7_five = inst[29]; func7_six = inst[30];
  //   func7_seven = inst[31]; JAL_type = Imm_3; MEM_WB = L_type; Imm_1 = MemRW; S_type = MemRW

  // Notes on the sheet:
  //   INPUTS to your circuit
  //   DON'T CHANGE THE LOCATIONS OF THE INPUTS AND OUTPUTS!
  //   OUTPUT from your circuit
endmodule
