// Logisim project cpu.circ as structural Verilog: 1 circuit, main circuit cpu
module cpu (
  input  clk,
  input  [31:0] INSTRUCTION,
  input  [31:0] READ_DATA,
  output [31:0] WRITE_ADDRESS,
  output [31:0] PROGRAM_COUNTER,
  output [31:0] ra,
  output [31:0] sp,
  output [31:0] t0,
  output [31:0] t1,
  output [31:0] t2,
  output [31:0] s0,
  output [31:0] s1,
  output [31:0] a0,
  output [31:0] tohost,
  output [3:0] WRITE_ENABLE,
  output [31:0] WRITE_DATA
);

  wire asel, breq, brlt, brun, bsel, csrsel, csrwe, PCSEL, regwen, WRITE_EN;
  wire [1:0] wbsel;
  wire [2:0] immsel;
  wire [3:0] alusel, multiplexer_5_out;
  wire [31:0] adder_1_out, csr_din, imm, INSTR, multiplexer_1_out, multiplexer_3_out, multiplexer_4_out, PC,
       PC4, RD, rd1, SELECT_PC, SIGN_BYTE, SIGN_WORD, WD;

  Register #(.width(32)) register_1 (.D(SELECT_PC), .clk(clk), .Q(INSTR));  // open: en, clr
  Adder #(.width(32)) adder_1 (.a(PROGRAM_COUNTER), .b(32'h4), .out(adder_1_out));  // open: cin, cout
  Register #(.width(32)) u_PC (.D(multiplexer_1_out), .clk(clk), .Q(PROGRAM_COUNTER));  // open: en, clr
  Multiplexer #(.enable("false"), .width(32)) multiplexer_1 (
    .in0(adder_1_out), .in1(WRITE_ADDRESS), .out(multiplexer_1_out), .sel(PCSEL));
  Multiplexer #(.enable("false"), .width(32)) multiplexer_2 (
    .in0(INSTRUCTION), .in1(32'h13), .out(SELECT_PC), .sel(PCSEL));
  Register #(.width(32)) register_2 (.D(PROGRAM_COUNTER), .clk(clk), .Q(PC));  // open: en, clr
  control_logic control_logic_1 (
    .CSRWen(csrwe), .PCSel(PCSEL), .RegWEn(regwen), .ImmSel(immsel), .BrUn(brun), .ASel(asel), .BSel(bsel),
    .ALUSel(alusel), .MemRW(WRITE_EN), .WBSel(wbsel), .CSRSel(csrsel), .inst(INSTR), .BrEq(breq), .BrLt(brlt));
  imm_gen imm_gen_1 (.inst(INSTR), .ImmSel(immsel), .imm(imm));
  regfile regfile_1 (
    .rs1(INSTR[19:15]), .rs2(INSTR[24:20]), .rd(INSTR[11:7]), .Write_Data(WD), .RegWEn(regwen), .clk(clk),
    .ra(ra), .sp(sp), .t0(t0), .t1(t1), .t2(t2), .s0(s0), .s1(s1), .a0(a0), .Read_Data_1(rd1),
    .Read_Data_2(WRITE_DATA));
  branch_comp branch_comp_1 (.rs1(rd1), .rs2(WRITE_DATA), .BrUn(brun), .BrEq(breq), .BrLt(brlt));
  Multiplexer #(.enable("false"), .width(32)) multiplexer_3 (.in0(PC), .in1(rd1), .out(multiplexer_3_out), .sel(asel));
  Multiplexer #(.enable("false"), .width(32)) multiplexer_4 (
    .in0(WRITE_DATA), .in1(imm), .out(multiplexer_4_out), .sel(bsel));
  alu alu_1 (.Result(WRITE_ADDRESS), .A(multiplexer_3_out), .B(multiplexer_4_out), .ALUSel(alusel));
  csr csr_1 (.CSR_address(12'h51e), .CSR_din(csr_din), .CSR_WE(csrwe), .clk(clk), .tohost(tohost));
  Multiplexer #(.enable("false"), .select(2), .width(4)) multiplexer_5 (
    .in0(4'b0001), .in1(4'b0011), .in2(4'b1111), .in3(4'b0000), .out(multiplexer_5_out), .sel(INSTR[13:12]));
  Multiplexer #(.enable("false"), .width(4)) multiplexer_6 (
    .in0(4'b0000), .in1(multiplexer_5_out), .out(WRITE_ENABLE), .sel(WRITE_EN));
  Adder #(.width(32)) adder_2 (.a(PC), .b(32'h4), .out(PC4));  // open: cin, cout
  Multiplexer #(.enable("false"), .width(32)) multiplexer_7 (.in0(rd1), .in1(imm), .out(csr_din), .sel(csrsel));
  Multiplexer #(.enable("false"), .select(2), .width(32)) multiplexer_8 (
    .in0(PC4), .in1(WRITE_ADDRESS), .in2(RD), .out(WD), .sel(wbsel));  // open: in3
  assign SIGN_BYTE = {{24{READ_DATA[7]}}, READ_DATA[7:0]};  // Bit_Extender bit_extender_1
  assign SIGN_WORD = {{16{READ_DATA[15]}}, READ_DATA[15:0]};  // Bit_Extender bit_extender_2
  Multiplexer #(.enable("false"), .select(2), .width(32)) multiplexer_9 (
    .in0(SIGN_BYTE), .in1(SIGN_WORD), .in2(READ_DATA), .in3({32{1'b0}}), .out(RD), .sel(INSTR[13:12]));

  // Other names for the same wires on the sheet: ALU_RES[31:0] = WRITE_ADDRESS; rd_t[4:0] = INSTR[11:7];
  //   MASK[1:0] = INSTR[13:12]; rs1[4:0] = INSTR[19:15]; rs2[4:0] = INSTR[24:20]; rd2[31:0] = WRITE_DATA;
  //   BYTE[7:0] = READ_DATA[7:0]; WORD[15:0] = READ_DATA[15:0]

  // Notes on the sheet:
  //   Output to IMEM
  //   IMEM (do **NOT** move this)
  //   Inputs from IMEM
  //   It is OK to move the PC, RegFile, ALU, MEM, Branch Comp, Imm Gen, and Control Logic to wherever is most convenient for you when constructing your CPU, and to delete this text
  //   Inputs/Outputs for testing. Do **NOT** move these.
  //   Outputs To DMEM
  //   DMEM (do **NOT** move this)
  //   Inputs From DMEM
endmodule
