// Logisim project imm_gen.circ as structural Verilog: 1 circuit, main circuit imm_gen
module imm_gen (
  input  [31:0] inst,
  input  [2:0] ImmSel,
  output [31:0] imm
);

  wire [31:0] Imm_inst_0, Imm_inst_1, Imm_inst_2, Imm_inst_3;

  assign Imm_inst_0 = {{20{inst[31]}}, inst[31:20]};  // Bit_Extender bit_extender_1
  assign Imm_inst_1 = {{20{inst[31]}}, {inst[31:25], inst[11:7]}};  // Bit_Extender bit_extender_2
  assign Imm_inst_2 = {{19{inst[31]}}, {inst[31], inst[7], inst[30:25], inst[11:8], 1'b0}};  // Bit_Extender bit_extender_3
  assign Imm_inst_3 = {{11{inst[31]}}, {inst[31], inst[19:12], inst[20], inst[30:21], 1'b0}};  // Bit_Extender bit_extender_4
  Multiplexer #(.enable("false"), .select(3), .width(32)) multiplexer_1 (
    .in0(Imm_inst_0), .in1(Imm_inst_1), .in2(Imm_inst_2), .in3(Imm_inst_3), .in4({inst[31:12], {12{1'b0}}}),
    .in5({{27{1'b0}}, inst[19:15]}), .in6({{27{1'b0}}, inst[19:15]}), .in7({{27{1'b0}}, inst[19:15]}),
    .out(imm), .sel(ImmSel));

  // Other names for the same wires on the sheet: Imm_inst_4[31:12] = inst[31:12]; Imm_inst_5[4:0] = inst[19:15]

  // Notes on the sheet:
  //   INPUTS to your circuit
  //   DON'T CHANGE THE LOCATIONS OF THE INPUTS AND OUTPUTS!
  //   OUTPUT from your circuit
endmodule
