// Logisim project regfile.circ as structural Verilog: 1 circuit, main circuit regfile
module regfile (
  input  [4:0] rs1,
  input  [4:0] rs2,
  input  [4:0] rd,
  input  [31:0] Write_Data,
  input  RegWEn,
  input  clk,
  output [31:0] ra,
  output [31:0] sp,
  output [31:0] t0,
  output [31:0] t1,
  output [31:0] t2,
  output [31:0] s0,
  output [31:0] s1,
  output [31:0] a0,
  output [31:0] Read_Data_1,
  output [31:0] Read_Data_2
);

  wire we0, we1, we2, we3, we4, we5, we6, we7, we8, we9, we10, we11, we12, we13, we14, we15, we16, we17,
       we18, we19, we20, we21, we22, we23, we24, we25, we26, we27, we28, we29, we30, we31;
  wire [31:0] reg3, reg4, reg11, reg12, reg13, reg14, reg15, reg16, reg17, reg18, reg19, reg20, reg21, reg22,
       reg23, reg24, reg25, reg26, reg27, reg28, reg29, reg30, reg31;

  Register #(.width(32)) register_1 (.D(Write_Data), .en(we8), .clk(clk), .Q(s0));  // open: clr
  Register #(.width(32)) register_2 (.D(Write_Data), .en(we10), .clk(clk), .Q(a0));  // open: clr
  Register #(.width(32)) register_3 (.D(Write_Data), .en(we12), .clk(clk), .Q(reg12));  // open: clr
  Register #(.width(32)) register_4 (.D(Write_Data), .en(we14), .clk(clk), .Q(reg14));  // open: clr
  Register #(.width(32)) register_5 (.D(Write_Data), .en(we16), .clk(clk), .Q(reg16));  // open: clr
  Register #(.width(32)) register_6 (.D(Write_Data), .en(we18), .clk(clk), .Q(reg18));  // open: clr
  Register #(.width(32)) register_7 (.D(Write_Data), .en(we1), .clk(clk), .Q(ra));  // open: clr
  Register #(.width(32)) register_8 (.D(Write_Data), .en(we9), .clk(clk), .Q(s1));  // open: clr
  Register #(.width(32)) register_9 (.D(Write_Data), .en(we11), .clk(clk), .Q(reg11));  // open: clr
  Register #(.width(32)) register_10 (.D(Write_Data), .en(we13), .clk(clk), .Q(reg13));  // open: clr
  Register #(.width(32)) register_11 (.D(Write_Data), .en(we15), .clk(clk), .Q(reg15));  // open: clr
  Register #(.width(32)) register_12 (.D(Write_Data), .en(we17), .clk(clk), .Q(reg17));  // open: clr
  Register #(.width(32)) register_13 (.D(Write_Data), .en(we19), .clk(clk), .Q(reg19));  // open: clr
  Register #(.width(32)) register_14 (.D(Write_Data), .en(we2), .clk(clk), .Q(sp));  // open: clr
  Demultiplexer #(.enable("false"), .select(5)) demultiplexer_1 (
    .out0(we0), .out1(we1), .out2(we2), .out3(we3), .out4(we4), .out5(we5), .out6(we6), .out7(we7),
    .out8(we8), .out9(we9), .out10(we10), .out11(we11), .out12(we12), .out13(we13), .out14(we14),
    .out15(we15), .out16(we16), .out17(we17), .out18(we18), .out19(we19), .out20(we20), .out21(we21),
    .out22(we22), .out23(we23), .out24(we24), .out25(we25), .out26(we26), .out27(we27), .out28(we28),
    .out29(we29), .out30(we30), .out31(we31), .in(RegWEn), .sel(rd));
  Register #(.width(32)) register_15 (.D(Write_Data), .en(we3), .clk(clk), .Q(reg3));  // open: clr
  Multiplexer #(.enable("false"), .select(5), .width(32)) multiplexer_1 (
    .in0({32{1'b0}}), .in1(ra), .in2(sp), .in3(reg3), .in4(reg4), .in5(t0), .in6(t1), .in7(t2), .in8(s0),
    .in9(s1), .in10(a0), .in11(reg11), .in12(reg12), .in13(reg13), .in14(reg14), .in15(reg15), .in16(reg16),
    .in17(reg17), .in18(reg18), .in19(reg19), .in20(reg20), .in21(reg21), .in22(reg22), .in23(reg23),
    .in24(reg24), .in25(reg25), .in26(reg26), .in27(reg27), .in28(reg28), .in29(reg29), .in30(reg30),
    .in31(reg31), .out(Read_Data_1), .sel(rs1));
  Register #(.width(32)) register_16 (.D(Write_Data), .en(we4), .clk(clk), .Q(reg4));  // open: clr
  Register #(.width(32)) register_17 (.D(Write_Data), .en(we20), .clk(clk), .Q(reg20));  // open: clr
  Register #(.width(32)) register_18 (.D(Write_Data), .en(we22), .clk(clk), .Q(reg22));  // open: clr
  Register #(.width(32)) register_19 (.D(Write_Data), .en(we24), .clk(clk), .Q(reg24));  // open: clr
  Register #(.width(32)) register_20 (.D(Write_Data), .en(we26), .clk(clk), .Q(reg26));  // open: clr
  Register #(.width(32)) register_21 (.D(Write_Data), .en(we28), .clk(clk), .Q(reg28));  // open: clr
  Register #(.width(32)) register_22 (.D(Write_Data), .en(we30), .clk(clk), .Q(reg30));  // open: clr
  Register #(.width(32)) register_23 (.D(Write_Data), .en(we5), .clk(clk), .Q(t0));  // open: clr
  Register #(.width(32)) register_24 (.D(Write_Data), .en(we21), .clk(clk), .Q(reg21));  // open: clr
  Register #(.width(32)) register_25 (.D(Write_Data), .en(we23), .clk(clk), .Q(reg23));  // open: clr
  Register #(.width(32)) register_26 (.D(Write_Data), .en(we25), .clk(clk), .Q(reg25));  // open: clr
  Register #(.width(32)) register_27 (.D(Write_Data), .en(we27), .clk(clk), .Q(reg27));  // open: clr
  Register #(.width(32)) register_28 (.D(Write_Data), .en(we29), .clk(clk), .Q(reg29));  // open: clr
  Register #(.width(32)) register_29 (.D(Write_Data), .en(we31), .clk(clk), .Q(reg31));  // open: clr
  Register #(.width(32)) register_30 (.D(Write_Data), .en(we6), .clk(clk), .Q(t1));  // open: clr
  Register #(.width(32)) register_31 (.D(Write_Data), .en(we7), .clk(clk), .Q(t2));  // open: clr
  Multiplexer #(.enable("false"), .select(5), .width(32)) multiplexer_2 (
    .in0({32{1'b0}}), .in1(ra), .in2(sp), .in3(reg3), .in4(reg4), .in5(t0), .in6(t1), .in7(t2), .in8(s0),
    .in9(s1), .in10(a0), .in11(reg11), .in12(reg12), .in13(reg13), .in14(reg14), .in15(reg15), .in16(reg16),
    .in17(reg17), .in18(reg18), .in19(reg19), .in20(reg20), .in21(reg21), .in22(reg22), .in23(reg23),
    .in24(reg24), .in25(reg25), .in26(reg26), .in27(reg27), .in28(reg28), .in29(reg29), .in30(reg30),
    .in31(reg31), .out(Read_Data_2), .sel(rs2));

  // Other names for the same wires on the sheet: read_data1[31:0] = Read_Data_1; read_data2[31:0] = Read_Data_2;
  //   read_reg1[4:0] = rs1; read_reg2[4:0] = rs2; reg1[31:0] = ra; reg2[31:0] = sp; reg5[31:0] = t0; reg6[31:0] = t1;
  //   reg7[31:0] = t2; reg8[31:0] = s0; reg9[31:0] = s1; reg10[31:0] = a0; write_en = RegWEn; write_reg[4:0] = rd

  // Notes on the sheet:
  //   INPUTS to your circuit
  //   DON'T CHANGE THE LOCATIONS OF THE INPUTS AND OUTPUTS!
  //   These are DEBUG/TEST outputs from your circuit.
  //   OUTPUTS from your circuit
endmodule
